# Fritzing sketch alarme de temperatura (saved by Fritzing 0.9.3b)
breadboards: 1

parts:
  Componente1 = Arduino Uno (Rev3)
  J1 = Piezo Speaker
  T1 = LM35 Temperature Sensor [package="TO92 [THT]"]
  R1 = Resistor [tolerance=±5% resistance=220 package=THT]
  LED2 = LED - 5mm [color="Red (633nm)" package="5 mm [THT]"]

nets:
  N1: Componente1.A0, T1.Vout
  N2: Componente1.D8, J1.pin2
  N3: Componente1.5V, T1.+Vs
  N4: J1.pin1, T1.GND, LED2.anode
  N5: R1.Pin_1, LED2.cathode
